# Fritzing sketch MP3DoorBell (saved by Fritzing 0.9.3b)

parts:
  DFPlayer_Mini1 = DFPlayer MINI [package="DIP (Dual Inline) [THT]"]
  Часть1 = Arduino Nano (Rev3.0)
  R2 = Resistor [tolerance=±5% resistance=1k package=THT]
  R3 = Resistor [tolerance=±5% resistance=1k package=THT]
  S1 = Pushbutton [package="[THT]"]
  R4 = Resistor [tolerance=±5% resistance=10k package=THT]  # not connected
  S2 = Reed switch [package=THT]
  Power_plug1 = Power plug
  R5 = Resistor [tolerance=±5% resistance=220 package=THT]  # not connected
  R6 = Resistor [tolerance=±5% resistance=10k package=THT]
  SP1 = SPEAKER [package=pcb_mount_speaker]
  LED1 = LED - 5mm [color="Green (570nm)" package="5 mm [THT]"]  # not connected
  R1 = Resistor [tolerance=±5% resistance=220 package=THT]  # not connected
  LED1_2 = LED - 5mm [color="Blue (525nm)" package="5 mm [THT]"]
  R7 = Resistor [tolerance=±5% resistance=10k package=THT]
  C1 = Ceramic Capacitor [capacitance=100nF package="100 mil [THT, multilayer]"]

nets:
  VCC: DFPlayer_Mini1.VCC, Часть1.5V, Power_plug1.VCC
  N1: DFPlayer_Mini1.RX, R3.Pin_1
  N2: DFPlayer_Mini1.TX, R2.Pin_1
  N3: DFPlayer_Mini1.SPK1, SP1.-
  GND: DFPlayer_Mini1.GND, Часть1.GND, Power_plug1.GND
  N4: DFPlayer_Mini1.SPK2, SP1.+
  N5: DFPlayer_Mini1.BUSY, Часть1.D3
  N6: Часть1.D2, S1.Pin_1, S1.Pin_2, R7.Pin_1, C1.1
  N7: Часть1.D4, S2.pin_2, R6.Pin_1
  N8: Часть1.D5, LED1_2.anode
  N9: Часть1.D10, R2.Pin_0
  N10: Часть1.D11/MOSI, R3.Pin_0
  N11: S1.Pin_4, C1.0

notes:
  + 5 В

custom parts:
  DFPlayer MINI: MP3 module by DFRobot.com for playing Music from an SD-Card. Supports WAV and MP3 files.
